// Logisim project practice_logisim.circ as structural Verilog: 1 circuit, main circuit main
module main (
  input  enable,
  input  in_2,
  input  in_3,
  input  in_4,
  input  in_5,
  input  in_6,
  input  in_7,
  input  in_8,
  input  D,
  input  en,
  input  in_11,
  output A0,
  output A1,
  output out_14,
  output A2,
  output A3,
  output out_17,
  output Q,
  output b0,
  output b1,
  output b2,
  output b3
);

  wire adder_1_cout, adder_1_out, adder_2_cout, adder_2_out, adder_3_cout, adder_3_out, adder_4_out,
       adder_5_cout, adder_5_out, adder_6_cout, adder_6_out, adder_7_cout, adder_7_out, adder_8_out, clk_out,
       clock_1_out, clock_2_out, d_ff_1_q, d_ff_2_q, d_ff_3_q, multiplexer_2_out, not_1_out, not_2_out;

  // Probe on multiplexer_2_out
  Clock clk (.out(clk_out));
  not not_1 (not_1_out, in_2);
  Multiplexer multiplexer_1 (.in0(out_17), .in1(in_6), .out(out_17), .sel(in_7));
  Multiplexer multiplexer_2 (.in0(D), .in1(multiplexer_2_out), .out(multiplexer_2_out), .sel(clk_out));
  // Probe on clk_out
  // Transmission_Gate transmission_1: pin names not known; wires that end beside it: in_3, in_2, not_1_out, out_14
  // Transmission_Gate transmission_2: pin names not known; wires that end beside it: in_4, not_1_out, in_5, out_14
  not not_2 (not_2_out, clk_out);
  Multiplexer multiplexer_3 (.in0(multiplexer_2_out), .in1(Q), .out(Q), .sel(not_2_out));
  Adder #(.width(1)) adder_1 (.a(b0), .b(en), .out(adder_1_out), .cin(1'b1), .cout(adder_1_cout));
  Adder #(.width(1)) adder_2 (.a(b1), .b(adder_1_cout), .out(adder_2_out), .cin(d_ff_1_q), .cout(adder_2_cout));
  Adder #(.width(1)) adder_3 (.a(b2), .b(adder_2_cout), .out(adder_3_out), .cin(d_ff_2_q), .cout(adder_3_cout));
  Adder #(.width(1)) adder_4 (.a(b3), .b(adder_3_cout), .out(adder_4_out), .cin(d_ff_3_q));  // open: cout
  Adder #(.width(1)) adder_5 (.a(A0), .b(enable), .out(adder_5_out), .cout(adder_5_cout));  // open: cin
  Adder #(.width(1)) adder_6 (.a(A1), .b(adder_5_cout), .out(adder_6_out), .cout(adder_6_cout));  // open: cin
  Adder #(.width(1)) adder_7 (.a(A2), .b(adder_6_cout), .out(adder_7_out), .cout(adder_7_cout));  // open: cin
  Adder #(.width(1)) adder_8 (.a(A3), .b(adder_7_cout), .out(adder_8_out));  // open: cin, cout
  // Probe on clock_1_out
  Clock clock_1 (.out(clock_1_out));
  // Probe on clock_2_out
  D_Flip_Flop d_ff_1 (.D(adder_1_out), .clk(clock_1_out), .Q(d_ff_1_q), .Qn(b0), .reset(in_11));  // open: preset
  D_Flip_Flop d_ff_2 (.D(adder_2_out), .clk(clock_1_out), .Q(d_ff_2_q), .Qn(b1), .reset(in_11));  // open: preset
  D_Flip_Flop d_ff_3 (.D(adder_3_out), .clk(clock_1_out), .Q(d_ff_3_q), .Qn(b2), .reset(in_11));  // open: preset
  D_Flip_Flop d_ff_4 (.D(adder_4_out), .clk(clock_1_out), .Qn(b3), .reset(in_11));  // open: Q, preset
  D_Flip_Flop d_ff_5 (.D(adder_5_out), .clk(clock_2_out), .Q(A0), .reset(in_8));  // open: Qn, preset
  D_Flip_Flop d_ff_6 (.D(adder_6_out), .clk(clock_2_out), .Q(A1), .reset(in_8));  // open: Qn, preset
  D_Flip_Flop d_ff_7 (.D(adder_7_out), .clk(clock_2_out), .Q(A2), .reset(in_8));  // open: Qn, preset
  D_Flip_Flop d_ff_8 (.D(adder_8_out), .clk(clock_2_out), .Q(A3), .reset(in_8));  // open: Qn, preset
  Clock clock_2 (.out(clock_2_out));
endmodule
