// Logisim project full_adder_4bits.circ as structural Verilog: 1 circuit, main circuit main
module main (
  input  c_in,
  input  a0,
  input  b0,
  input  a1,
  input  b1,
  input  a2,
  input  b2,
  input  a3,
  input  b3,
  output sum3,
  output sum0,
  output sum1,
  output sum2,
  output c_out
);

  wire adder_1_cout, adder_2_cout, adder_3_cout;

  Adder #(.width(1)) adder_1 (.a(a0), .b(b0), .out(sum0), .cin(c_in), .cout(adder_1_cout));
  Adder #(.width(1)) adder_2 (.a(a1), .b(b1), .out(sum1), .cin(adder_1_cout), .cout(adder_2_cout));
  Adder #(.width(1)) adder_3 (.a(a2), .b(b2), .out(sum2), .cin(adder_2_cout), .cout(adder_3_cout));
  Adder #(.width(1)) adder_4 (.a(a3), .b(b3), .out(sum3), .cin(adder_3_cout), .cout(c_out));
endmodule
